# Fritzing sketch Programmer (saved by Fritzing 0.9.2b)
breadboards: 1

parts:
  U1 = ESP8266-12e_tht [part_number=ESP8266-12E]
  R1 = Resistor [tolerance=±5% resistance=10k package=THT]
  R2 = Resistor [tolerance=±5% resistance=10k package=THT]
  R3 = Resistor [tolerance=±5% resistance=10k package=THT]
  R4 = Resistor [tolerance=±5% resistance=10k package=THT]
  C2 = Electrolytic Capacitor [capacitance=0.47mF package="200 mil [THT, electrolytic]"]
  S1 = Momentary Switch [package=ksa_sealed_tac_switch]
  S2 = Momentary Switch [package=ksa_sealed_tac_switch]
  Part1 = FTDI Basic Programmer

nets:
  N1: U1.REST, S2.2
  N2: U1.CH_PD, R2.Pin_1
  N3: U1.VCC, R2.Pin_0, R3.Pin_0, R4.Pin_0, C2.+
  GND: U1.GND, R1.Pin_0, C2.-, S1.4, S2.4, Part1.GND
  N4: U1.GPIO_15, R1.Pin_1
  N5: U1.GPIO_0, S1.2
  N6: U1.GPIO_3/RXD, Part1.TXO
  N7: U1.GPIO_1/TXD, Part1.RXI
  N8: R3.Pin_1, S2.3
  N9: R4.Pin_1, S1.3

notes:
  reset
  flash
  +3.3V
  Ground

custom parts:
  ESP8266-12e_tht: These are the first series of modules made with the ESP8266 by the third-party manufacturer AI-Thinker and remain the most widely available. They are collectively referred to as "ESP-xx modules" and to form a workable development system require additional components, especially a serial TTL-to-USB adapter (sometimes called a USB-to-UART bridge) and an external 3.3V power supply. The pcb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
