# Fritzing sketch Receiver (saved by Fritzing 0.9.2b)
breadboards: 1

parts:
  B1 = Bolt WiFi Module [package=dip]
  Part1 = Arduino Uno (Rev3)
  U1 = LCD-16X2 [package=lcd-16x2_nosilk]
  R1 = TRIMPOT [package=3362u-2]
  R2 = Resistor [tolerance=±5% resistance=220 package=THT]

nets:
  GND: B1.pin1, Part1.GND, U1.VSS, U1.R_W, R1.CCW, R2.Pin_0
  N1: B1.pin8, Part1.D0/RX
  N2: B1.pin9, Part1.D1/TX
  N3: B1.pin11, U1.A
  N4: Part1.D8, U1.DB6
  N5: Part1.D9_PWM, U1.DB5
  N6: Part1.D10_PWM/SS, U1.DB4
  N7: Part1.D11_PWM/MOSI, U1.E
  N8: Part1.D12/MISO, U1.RS
  N9: Part1.D7, U1.DB7
  N10: Part1.3V3, R1.CW
  5V: Part1.5V, U1.VDD
  N11: U1.VO, R1.WIPER
  N12: U1.K, R2.Pin_1

custom parts:
  Bolt WiFi Module: Bolt IoT platform gives you the capability to control your devices and collect data from IoT devices safely and securely no matter where you are. Get actionable insights by deploying machine learning algorithms with just a few clicks to detect anomalies as well as predict sensor values.
