# Fritzing sketch Transmitter (saved by Fritzing 0.9.2b)
breadboards: 1

parts:
  U1 = ESP8266-12e_tht [part_number=ESP8266-12E]
  Part1 = Arduino Uno (Rev3) - ICSP
  R1 = Resistor [tolerance=±5% resistance=10k package=THT]
  R2 = Resistor [tolerance=±5% resistance=10k package=THT]
  R3 = Resistor [tolerance=±5% resistance=10k package=THT]
  R4 = Resistor [tolerance=±5% resistance=10k package=THT]
  C2 = Electrolytic Capacitor [capacitance=0.47mF package="200 mil [THT, electrolytic]"]
  S1 = Momentary Switch [package=ksa_sealed_tac_switch]
  S2 = Momentary Switch [package=ksa_sealed_tac_switch]
  R5 = Photocell (LDR) [package=THT]
  T1 = LM35 Temperature Sensor [package="TO92 [THT]"]
  R6 = Resistor [tolerance=±5% resistance=1k package=THT]
  R7 = Resistor [tolerance=±5% resistance=2.2k package=THT]
  R8 = Resistor [tolerance=±5% resistance=1k package=THT]

nets:
  N1: U1.REST, S2.2
  N2: U1.CH_PD, R2.Pin_1
  N3: U1.VCC, R2.Pin_0, R3.Pin_0, R4.Pin_0, C2.+
  GND: U1.GND, Part1.GND, R1.Pin_0, C2.-, S1.4, S2.4, T1.GND, R6.Pin_1, R7.Pin_1
  N4: U1.GPIO_15, R1.Pin_1
  N5: U1.GPIO_0, S1.2
  N6: U1.GPIO_3/RXD, R8.Pin_0
  N7: U1.GPIO_1/TXD, Part1.D0/RX
  N8: Part1.A0, R5.pin_1, R6.Pin_0
  N9: Part1.A1, T1.Vout
  N10: Part1.D1/TX, R7.Pin_0, R8.Pin_1
  N11: Part1.5V, R5.pin_0, T1.+Vs
  N12: R3.Pin_1, S2.3
  N13: R4.Pin_1, S1.3

notes:
  reset
  flash
  +3.3V
  Ground

custom parts:
  ESP8266-12e_tht: These are the first series of modules made with the ESP8266 by the third-party manufacturer AI-Thinker and remain the most widely available. They are collectively referred to as "ESP-xx modules" and to form a workable development system require additional components, especially a serial TTL-to-USB adapter (sometimes called a USB-to-UART bridge) and an external 3.3V power supply. The pcb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
